# Fritzing sketch V001-Nano_ESP32-PCB_25x25cmKlok (saved by Fritzing 1.0.5)
circuit board: 24.2178cm x 20.1674cm

parts:
  74AHCT125 = 74HC08 Logic AND Gate [part_number=74HC08 package="DIP (Dual Inline) [THT]"]
  C1 = Electrolytic Capacitor [capacitance=1mF voltage=35V package="100 mil [THT, electrolytic]"]
  Arduino_Nano_ESP32 = Arduino Nano (Rev3.0)
  RTCclock7 = female pin header, 3 pins [form="♀ (female)"]
  R14 = Resistor [tolerance=±5% resistance=470 power=0.25 package=THT]
  J2 = screw terminal, 2 pins
  RTC-clock = female pin header, 6 pins [form="♀ (female)"]
  LDR = male pin header, 2 pins [form="♂ (male)"]
  R15 = Resistor [tolerance=±5% resistance=10k power=0.25W package=THT]
  Rotary = female pin header, 5 pins [form="♀ (female)"]
  5V_Di_GND = SMD RGB LED (SK6812) [package=5050]
  5V_Di_GND1 = SMD RGB LED (SK6812) [package=5050]
  5V_Di_GND2 = SMD RGB LED (SK6812) [package=5050]
  5V_Di_GND3 = SMD RGB LED (SK6812) [package=5050]
  5V_Di_GND4 = SMD RGB LED (SK6812) [package=5050]
  5V_Di_GND5 = SMD RGB LED (SK6812) [package=5050]
  5V_Di_GND6 = SMD RGB LED (SK6812) [package=5050]
  5V_Di_GND7 = SMD RGB LED (SK6812) [package=5050]
  5V_Di_GND8 = SMD RGB LED (SK6812) [package=5050]
  5V_Di_GND9 = SMD RGB LED (SK6812) [package=5050]
  5V_Di_GND10 = SMD RGB LED (SK6812) [package=5050]
  5V_Di_GND24 = SMD RGB LED (SK6812) [package=5050]
  5V_Di_GND23 = SMD RGB LED (SK6812) [package=5050]
  5V_Di_GND22 = SMD RGB LED (SK6812) [package=5050]
  5V_Di_GND17 = SMD RGB LED (SK6812) [package=5050]
  5V_Di_GND21 = SMD RGB LED (SK6812) [package=5050]
  5V_Di_GND19 = SMD RGB LED (SK6812) [package=5050]
  5V_Di_GND18 = SMD RGB LED (SK6812) [package=5050]
  5V_Di_GND17_2 = SMD RGB LED (SK6812) [package=5050]
  5V_Di_GND15 = SMD RGB LED (SK6812) [package=5050]
  5V_Di_GND16 = SMD RGB LED (SK6812) [package=5050]
  5V_Di_GND14 = SMD RGB LED (SK6812) [package=5050]
  5V_Di_GND13 = SMD RGB LED (SK6812) [package=5050]
  5V_Di_GND34 = SMD RGB LED (SK6812) [package=5050]
  5V_Di_GND25 = SMD RGB LED (SK6812) [package=5050]
  5V_Di_GND26 = SMD RGB LED (SK6812) [package=5050]
  5V_Di_GND27 = SMD RGB LED (SK6812) [package=5050]
  5V_Di_GND28 = SMD RGB LED (SK6812) [package=5050]
  5V_Di_GND29 = SMD RGB LED (SK6812) [package=5050]
  5V_Di_GND30 = SMD RGB LED (SK6812) [package=5050]
  5V_Di_GND31 = SMD RGB LED (SK6812) [package=5050]
  5V_Di_GND32 = SMD RGB LED (SK6812) [package=5050]
  5V_Di_GND33 = SMD RGB LED (SK6812) [package=5050]
  5V_Di_GND47 = SMD RGB LED (SK6812) [package=5050]
  5V_Di_GND48 = SMD RGB LED (SK6812) [package=5050]
  5V_Di_GND46 = SMD RGB LED (SK6812) [package=5050]
  5V_Di_GND45 = SMD RGB LED (SK6812) [package=5050]
  5V_Di_GND44 = SMD RGB LED (SK6812) [package=5050]
  5V_Di_GND43 = SMD RGB LED (SK6812) [package=5050]
  5V_Di_GND42 = SMD RGB LED (SK6812) [package=5050]
  5V_Di_GND41 = SMD RGB LED (SK6812) [package=5050]
  5V_Di_GND40 = SMD RGB LED (SK6812) [package=5050]
  5V_Di_GND39 = SMD RGB LED (SK6812) [package=5050]
  5V_Di_GND38 = SMD RGB LED (SK6812) [package=5050]
  5V_Di_GND37 = SMD RGB LED (SK6812) [package=5050]
  5V_Di_GND71 = SMD RGB LED (SK6812) [package=5050]
  5V_Di_GND72 = SMD RGB LED (SK6812) [package=5050]
  5V_Di_GND95 = SMD RGB LED (SK6812) [package=5050]
  5V_Di_GND96 = SMD RGB LED (SK6812) [package=5050]
  5V_Di_GND52 = SMD RGB LED (SK6812) [package=5050]
  5V_Di_GND11 = SMD RGB LED (SK6812) [package=5050]
  5V_Di_GND12 = SMD RGB LED (SK6812) [package=5050]
  5V_Di_GND35 = SMD RGB LED (SK6812) [package=5050]
  5V_Di_GND36 = SMD RGB LED (SK6812) [package=5050]
  5V_Di_GND57 = SMD RGB LED (SK6812) [package=5050]
  5V_Di_GND58 = SMD RGB LED (SK6812) [package=5050]
  5V_Di_GND49 = SMD RGB LED (SK6812) [package=5050]
  5V_Di_GND50 = SMD RGB LED (SK6812) [package=5050]
  5V_Di_GND51 = SMD RGB LED (SK6812) [package=5050]
  5V_Di_GND52_2 = SMD RGB LED (SK6812) [package=5050]
  5V_Di_GND53 = SMD RGB LED (SK6812) [package=5050]
  5V_Di_GND54 = SMD RGB LED (SK6812) [package=5050]
  5V_Di_GND55 = SMD RGB LED (SK6812) [package=5050]
  5V_Di_GND56 = SMD RGB LED (SK6812) [package=5050]
  5V_Di_GND57_2 = SMD RGB LED (SK6812) [package=5050]
  5V_Di_GND58_2 = SMD RGB LED (SK6812) [package=5050]
  5V_Di_GND59 = SMD RGB LED (SK6812) [package=5050]
  5V_Di_GND60 = SMD RGB LED (SK6812) [package=5050]
  5V_Di_GND61 = SMD RGB LED (SK6812) [package=5050]
  5V_Di_GND62 = SMD RGB LED (SK6812) [package=5050]
  5V_Di_GND63 = SMD RGB LED (SK6812) [package=5050]
  5V_Di_GND64 = SMD RGB LED (SK6812) [package=5050]
  5V_Di_GND65 = SMD RGB LED (SK6812) [package=5050]
  5V_Di_GND70 = SMD RGB LED (SK6812) [package=5050]
  5V_Di_GND69 = SMD RGB LED (SK6812) [package=5050]
  5V_Di_GND68 = SMD RGB LED (SK6812) [package=5050]
  5V_Di_GND67 = SMD RGB LED (SK6812) [package=5050]
  5V_Di_GND66 = SMD RGB LED (SK6812) [package=5050]
  5V_Di_GND73 = SMD RGB LED (SK6812) [package=5050]
  5V_Di_GND74 = SMD RGB LED (SK6812) [package=5050]
  5V_Di_GND75 = SMD RGB LED (SK6812) [package=5050]
  5V_Di_GND76 = SMD RGB LED (SK6812) [package=5050]
  5V_Di_GND77 = SMD RGB LED (SK6812) [package=5050]
  5V_Di_GND78 = SMD RGB LED (SK6812) [package=5050]
  5V_Di_GND79 = SMD RGB LED (SK6812) [package=5050]
  5V_Di_GND80 = SMD RGB LED (SK6812) [package=5050]
  5V_Di_GND81 = SMD RGB LED (SK6812) [package=5050]
  5V_Di_GND82 = SMD RGB LED (SK6812) [package=5050]
  5V_Di_GND83 = SMD RGB LED (SK6812) [package=5050]
  5V_Di_GND94 = SMD RGB LED (SK6812) [package=5050]  # not connected
  5V_Di_GND93 = SMD RGB LED (SK6812) [package=5050]  # not connected
  5V_Di_GND92 = SMD RGB LED (SK6812) [package=5050]  # not connected
  5V_Di_GND91 = SMD RGB LED (SK6812) [package=5050]  # not connected
  5V_Di_GND90 = SMD RGB LED (SK6812) [package=5050]  # not connected
  5V_Di_GND89 = SMD RGB LED (SK6812) [package=5050]  # not connected
  5V_Di_GND88 = SMD RGB LED (SK6812) [package=5050]  # not connected
  5V_Di_GND87 = SMD RGB LED (SK6812) [package=5050]  # not connected
  5V_Di_GND86 = SMD RGB LED (SK6812) [package=5050]  # not connected
  5V_Di_GND85 = SMD RGB LED (SK6812) [package=5050]  # not connected
  5V_Di_GND84 = SMD RGB LED (SK6812) [package=5050]
  5V_Di_GND103 = SMD RGB LED (SK6812) [package=5050]
  5V_Di_GND104 = SMD RGB LED (SK6812) [package=5050]  # not connected
  5V_Di_GND105 = SMD RGB LED (SK6812) [package=5050]  # not connected
  5V_Di_GND106 = SMD RGB LED (SK6812) [package=5050]  # not connected
  5V_Di_GND107 = SMD RGB LED (SK6812) [package=5050]  # not connected
  5V_Di_GND108 = SMD RGB LED (SK6812) [package=5050]  # not connected
  5V_Di_GND109 = SMD RGB LED (SK6812) [package=5050]  # not connected
  5V_Di_GND110 = SMD RGB LED (SK6812) [package=5050]  # not connected
  5V_Di_GND111 = SMD RGB LED (SK6812) [package=5050]  # not connected
  5V_Di_GND112 = SMD RGB LED (SK6812) [package=5050]  # not connected
  5V_Di_GND113 = SMD RGB LED (SK6812) [package=5050]  # not connected
  5V_Di_GND114 = SMD RGB LED (SK6812) [package=5050]  # not connected
  5V_Di_GND115 = SMD RGB LED (SK6812) [package=5050]  # not connected
  5V_Di_GND116 = SMD RGB LED (SK6812) [package=5050]  # not connected
  5V_Di_GND117 = SMD RGB LED (SK6812) [package=5050]  # not connected
  5V_Di_GND118 = SMD RGB LED (SK6812) [package=5050]  # not connected
  5V_Di_GND119 = SMD RGB LED (SK6812) [package=5050]  # not connected
  5V_Di_GND120 = SMD RGB LED (SK6812) [package=5050]  # not connected
  5V_Di_GND121 = SMD RGB LED (SK6812) [package=5050]  # not connected
  5V_Di_GND122 = SMD RGB LED (SK6812) [package=5050]  # not connected
  5V_Di_GND123 = SMD RGB LED (SK6812) [package=5050]  # not connected
  5V_Di_GND124 = SMD RGB LED (SK6812) [package=5050]
  5V_Di_GND125 = SMD RGB LED (SK6812) [package=5050]  # not connected
  5V_Di_GND126 = SMD RGB LED (SK6812) [package=5050]  # not connected
  5V_Di_GND127 = SMD RGB LED (SK6812) [package=5050]  # not connected
  5V_Di_GND128 = SMD RGB LED (SK6812) [package=5050]  # not connected
  5V_Di_GND129 = SMD RGB LED (SK6812) [package=5050]  # not connected
  5V_Di_GND130 = SMD RGB LED (SK6812) [package=5050]  # not connected
  5V_Di_GND131 = SMD RGB LED (SK6812) [package=5050]  # not connected
  5V_Di_GND132 = SMD RGB LED (SK6812) [package=5050]  # not connected
  5V_Di_GND133 = SMD RGB LED (SK6812) [package=5050]  # not connected
  5V_Di_GND134 = SMD RGB LED (SK6812) [package=5050]  # not connected
  5V_Di_GND135 = SMD RGB LED (SK6812) [package=5050]
  5V_Di_GND136 = SMD RGB LED (SK6812) [package=5050]  # not connected
  5V_Di_GND137 = SMD RGB LED (SK6812) [package=5050]  # not connected
  5V_Di_GND138 = SMD RGB LED (SK6812) [package=5050]  # not connected
  5V_Di_GND139 = SMD RGB LED (SK6812) [package=5050]  # not connected
  5V_Di_GND140 = SMD RGB LED (SK6812) [package=5050]  # not connected
  5V_Di_GND141 = SMD RGB LED (SK6812) [package=5050]  # not connected
  5V_Di_GND142 = SMD RGB LED (SK6812) [package=5050]  # not connected
  5V_Di_GND143 = SMD RGB LED (SK6812) [package=5050]  # not connected
  5V_Di_GND144 = SMD RGB LED (SK6812) [package=5050]  # not connected
  5V_Di_GND145 = SMD RGB LED (SK6812) [package=5050]  # not connected
  5V_Di_GND146 = SMD RGB LED (SK6812) [package=5050]
  LDR_GL5516 = Photocell (LDR) [power=0.25W dark_resistance_@0.01lx=300kΩ light_resistance_@100lx=400Ω luminance=10lx package=THT]
  1N5818 = Rectifier Diode [part_number=1N4001 package="300 mil [THT]"]
  RTCclock8 = female pin header, 3 pins [form="♀ (female)"]

nets:
  GND: 74AHCT125.1A, C1.-, Arduino_Nano_ESP32.GND, RTCclock7.pin3, J2.pin1, RTC-clock.pin1, R15.Pin_1, Rotary.pin1, 5V_Di_GND.GND, 5V_Di_GND1.GND, 5V_Di_GND2.GND, 5V_Di_GND3.GND, 5V_Di_GND4.GND, 5V_Di_GND5.GND, 5V_Di_GND6.GND, 5V_Di_GND7.GND, 5V_Di_GND8.GND, 5V_Di_GND9.GND, 5V_Di_GND10.GND, 5V_Di_GND24.GND, 5V_Di_GND23.GND, 5V_Di_GND22.GND, 5V_Di_GND17.GND, 5V_Di_GND21.GND, 5V_Di_GND19.GND, 5V_Di_GND18.GND, 5V_Di_GND17_2.GND, 5V_Di_GND15.GND, 5V_Di_GND16.GND, 5V_Di_GND14.GND, 5V_Di_GND13.GND, 5V_Di_GND34.GND, 5V_Di_GND25.GND, 5V_Di_GND26.GND, 5V_Di_GND27.GND, 5V_Di_GND28.GND, 5V_Di_GND29.GND, 5V_Di_GND30.GND, 5V_Di_GND31.GND, 5V_Di_GND32.GND, 5V_Di_GND33.GND, 5V_Di_GND47.GND, 5V_Di_GND48.GND, 5V_Di_GND46.GND, 5V_Di_GND45.GND, 5V_Di_GND44.GND, 5V_Di_GND43.GND, 5V_Di_GND42.GND, 5V_Di_GND41.GND, 5V_Di_GND40.GND, 5V_Di_GND39.GND, 5V_Di_GND38.GND, 5V_Di_GND37.GND, 5V_Di_GND71.GND, 5V_Di_GND72.GND, 5V_Di_GND95.GND, 5V_Di_GND96.GND, 5V_Di_GND52.GND, 5V_Di_GND11.GND, 5V_Di_GND12.GND, 5V_Di_GND35.GND, 5V_Di_GND36.GND, 5V_Di_GND57.GND, 5V_Di_GND58.GND, 5V_Di_GND49.GND, 5V_Di_GND50.GND, 5V_Di_GND51.GND, 5V_Di_GND52_2.GND, 5V_Di_GND53.GND, 5V_Di_GND54.GND, 5V_Di_GND55.GND, 5V_Di_GND56.GND, 5V_Di_GND57_2.GND, 5V_Di_GND58_2.GND, 5V_Di_GND59.GND, 5V_Di_GND60.GND, 5V_Di_GND61.GND, 5V_Di_GND62.GND, 5V_Di_GND63.GND, 5V_Di_GND64.GND, 5V_Di_GND65.GND, 5V_Di_GND70.GND, 5V_Di_GND69.GND, 5V_Di_GND68.GND, 5V_Di_GND67.GND, 5V_Di_GND66.GND, 5V_Di_GND73.GND, 5V_Di_GND74.GND, 5V_Di_GND75.GND, 5V_Di_GND76.GND, 5V_Di_GND77.GND, 5V_Di_GND78.GND, 5V_Di_GND79.GND, 5V_Di_GND80.GND, 5V_Di_GND81.GND, 5V_Di_GND82.GND, 5V_Di_GND83.GND, 5V_Di_GND84.GND, RTCclock8.pin3
  N1: 74AHCT125.1B, Arduino_Nano_ESP32.D5
  N2: 74AHCT125.1Y, R14.Pin_0
  VCC: 74AHCT125.VCC, C1.+, RTCclock7.pin1, J2.pin2, 5V_Di_GND.VCC, 5V_Di_GND1.VCC, 5V_Di_GND2.VCC, 5V_Di_GND3.VCC, 5V_Di_GND4.VCC, 5V_Di_GND5.VCC, 5V_Di_GND6.VCC, 5V_Di_GND7.VCC, 5V_Di_GND8.VCC, 5V_Di_GND9.VCC, 5V_Di_GND10.VCC, 5V_Di_GND24.VCC, 5V_Di_GND23.VCC, 5V_Di_GND22.VCC, 5V_Di_GND17.VCC, 5V_Di_GND21.VCC, 5V_Di_GND19.VCC, 5V_Di_GND18.VCC, 5V_Di_GND17_2.VCC, 5V_Di_GND15.VCC, 5V_Di_GND16.VCC, 5V_Di_GND14.VCC, 5V_Di_GND13.VCC, 5V_Di_GND34.VCC, 5V_Di_GND25.VCC, 5V_Di_GND26.VCC, 5V_Di_GND27.VCC, 5V_Di_GND28.VCC, 5V_Di_GND29.VCC, 5V_Di_GND30.VCC, 5V_Di_GND31.VCC, 5V_Di_GND32.VCC, 5V_Di_GND33.VCC, 5V_Di_GND47.VCC, 5V_Di_GND48.VCC, 5V_Di_GND46.VCC, 5V_Di_GND45.VCC, 5V_Di_GND44.VCC, 5V_Di_GND43.VCC, 5V_Di_GND42.VCC, 5V_Di_GND41.VCC, 5V_Di_GND40.VCC, 5V_Di_GND39.VCC, 5V_Di_GND38.VCC, 5V_Di_GND37.VCC, 5V_Di_GND71.VCC, 5V_Di_GND72.VCC, 5V_Di_GND11.VCC, 5V_Di_GND12.VCC, 5V_Di_GND35.VCC, 5V_Di_GND36.VCC, 5V_Di_GND49.VCC, 5V_Di_GND50.VCC, 5V_Di_GND51.VCC, 5V_Di_GND52_2.VCC, 5V_Di_GND53.VCC, 5V_Di_GND54.VCC, 5V_Di_GND55.VCC, 5V_Di_GND56.VCC, 5V_Di_GND57_2.VCC, 5V_Di_GND58_2.VCC, 5V_Di_GND59.VCC, 5V_Di_GND60.VCC, 5V_Di_GND61.VCC, 5V_Di_GND62.VCC, 5V_Di_GND63.VCC, 5V_Di_GND64.VCC, 5V_Di_GND65.VCC, 5V_Di_GND70.VCC, 5V_Di_GND69.VCC, 5V_Di_GND68.VCC, 5V_Di_GND67.VCC, 5V_Di_GND66.VCC, 5V_Di_GND73.VCC, 5V_Di_GND74.VCC, 5V_Di_GND75.VCC, 5V_Di_GND76.VCC, 5V_Di_GND77.VCC, 5V_Di_GND78.VCC, 5V_Di_GND79.VCC, 5V_Di_GND80.VCC, 5V_Di_GND81.VCC, 5V_Di_GND82.VCC, 5V_Di_GND83.VCC, 5V_Di_GND84.VCC, 5V_Di_GND103.VCC, 5V_Di_GND124.VCC, 5V_Di_GND135.VCC, 5V_Di_GND146.VCC, 1N5818.anode
  N3: Arduino_Nano_ESP32.D2, Rotary.pin5
  N4: Arduino_Nano_ESP32.D3, Rotary.pin4
  N5: Arduino_Nano_ESP32.D4, Rotary.pin3
  N6: Arduino_Nano_ESP32.5V, 1N5818.cathode
  N7: Arduino_Nano_ESP32.A5, RTC-clock.pin4
  N8: Arduino_Nano_ESP32.A4, RTC-clock.pin3
  N9: Arduino_Nano_ESP32.A2, LDR.pin2, R15.Pin_0, LDR_GL5516.pin_0
  N10: Arduino_Nano_ESP32.3V3, RTC-clock.pin2, LDR.pin1, Rotary.pin2, LDR_GL5516.pin_1
  N11: RTCclock7.pin2, R14.Pin_1, 5V_Di_GND.DIn
  N12: 5V_Di_GND.DOut, 5V_Di_GND1.DIn
  N13: 5V_Di_GND1.DOut, 5V_Di_GND2.DIn
  N14: 5V_Di_GND2.DOut, 5V_Di_GND3.DIn
  N15: 5V_Di_GND3.DOut, 5V_Di_GND4.DIn
  N16: 5V_Di_GND4.DOut, 5V_Di_GND5.DIn
  N17: 5V_Di_GND5.DOut, 5V_Di_GND6.DIn
  N18: 5V_Di_GND6.DOut, 5V_Di_GND7.DIn
  N19: 5V_Di_GND7.DOut, 5V_Di_GND8.DIn
  N20: 5V_Di_GND8.DOut, 5V_Di_GND9.DIn
  N21: 5V_Di_GND9.DOut, 5V_Di_GND10.DIn
  N22: 5V_Di_GND10.DOut, 5V_Di_GND11.DIn
  N23: 5V_Di_GND24.DIn, 5V_Di_GND23.DOut
  N24: 5V_Di_GND24.DOut, 5V_Di_GND25.DIn
  N25: 5V_Di_GND23.DIn, 5V_Di_GND22.DOut
  N26: 5V_Di_GND22.DIn, 5V_Di_GND17.DOut
  N27: 5V_Di_GND17.DIn, 5V_Di_GND21.DOut
  N28: 5V_Di_GND21.DIn, 5V_Di_GND19.DOut
  N29: 5V_Di_GND19.DIn, 5V_Di_GND18.DOut
  N30: 5V_Di_GND18.DIn, 5V_Di_GND17_2.DOut
  N31: 5V_Di_GND17_2.DIn, 5V_Di_GND15.DOut
  N32: 5V_Di_GND15.DIn, 5V_Di_GND16.DOut
  N33: 5V_Di_GND16.DIn, 5V_Di_GND14.DOut
  N34: 5V_Di_GND14.DIn, 5V_Di_GND13.DOut
  N35: 5V_Di_GND13.DIn, 5V_Di_GND12.DOut
  N36: 5V_Di_GND34.DIn, 5V_Di_GND33.DOut
  N37: 5V_Di_GND34.DOut, 5V_Di_GND35.DIn
  N38: 5V_Di_GND25.DOut, 5V_Di_GND26.DIn
  N39: 5V_Di_GND26.DOut, 5V_Di_GND27.DIn
  N40: 5V_Di_GND27.DOut, 5V_Di_GND28.DIn
  N41: 5V_Di_GND28.DOut, 5V_Di_GND29.DIn
  N42: 5V_Di_GND29.DOut, 5V_Di_GND30.DIn
  N43: 5V_Di_GND30.DOut, 5V_Di_GND31.DIn
  N44: 5V_Di_GND31.DOut, 5V_Di_GND32.DIn
  N45: 5V_Di_GND32.DOut, 5V_Di_GND33.DIn
  N46: 5V_Di_GND47.DIn, 5V_Di_GND46.DOut
  N47: 5V_Di_GND47.DOut, 5V_Di_GND48.DIn
  N48: 5V_Di_GND48.DOut, 5V_Di_GND49.DIn
  N49: 5V_Di_GND46.DIn, 5V_Di_GND45.DOut
  N50: 5V_Di_GND45.DIn, 5V_Di_GND44.DOut
  N51: 5V_Di_GND44.DIn, 5V_Di_GND43.DOut
  N52: 5V_Di_GND43.DIn, 5V_Di_GND42.DOut
  N53: 5V_Di_GND42.DIn, 5V_Di_GND41.DOut
  N54: 5V_Di_GND41.DIn, 5V_Di_GND40.DOut
  N55: 5V_Di_GND40.DIn, 5V_Di_GND39.DOut
  N56: 5V_Di_GND39.DIn, 5V_Di_GND38.DOut
  N57: 5V_Di_GND38.DIn, 5V_Di_GND37.DOut
  N58: 5V_Di_GND37.DIn, 5V_Di_GND36.DOut
  N59: 5V_Di_GND71.DIn, 5V_Di_GND70.DOut
  N60: 5V_Di_GND71.DOut, 5V_Di_GND72.DIn
  N61: 5V_Di_GND72.DOut, 5V_Di_GND73.DIn
  VCC_2: 5V_Di_GND95.VCC, 5V_Di_GND96.VCC
  N62: 5V_Di_GND95.DOut, 5V_Di_GND96.DIn
  VCC_3: 5V_Di_GND52.VCC, 5V_Di_GND57.VCC
  N63: 5V_Di_GND52.DOut, 5V_Di_GND57.DIn
  N64: 5V_Di_GND11.DOut, 5V_Di_GND12.DIn
  N65: 5V_Di_GND35.DOut, 5V_Di_GND36.DIn
  N66: 5V_Di_GND58.VCC, RTCclock8.pin1
  N67: 5V_Di_GND58.DOut, RTCclock8.pin2
  N68: 5V_Di_GND49.DOut, 5V_Di_GND50.DIn
  N69: 5V_Di_GND50.DOut, 5V_Di_GND51.DIn
  N70: 5V_Di_GND51.DOut, 5V_Di_GND52_2.DIn
  N71: 5V_Di_GND52_2.DOut, 5V_Di_GND53.DIn
  N72: 5V_Di_GND53.DOut, 5V_Di_GND54.DIn
  N73: 5V_Di_GND54.DOut, 5V_Di_GND55.DIn
  N74: 5V_Di_GND55.DOut, 5V_Di_GND56.DIn
  N75: 5V_Di_GND56.DOut, 5V_Di_GND57_2.DIn
  N76: 5V_Di_GND57_2.DOut, 5V_Di_GND58_2.DIn
  N77: 5V_Di_GND58_2.DOut, 5V_Di_GND59.DIn
  N78: 5V_Di_GND59.DOut, 5V_Di_GND60.DIn
  N79: 5V_Di_GND60.DOut, 5V_Di_GND61.DIn
  N80: 5V_Di_GND61.DOut, 5V_Di_GND62.DIn
  N81: 5V_Di_GND62.DOut, 5V_Di_GND63.DIn
  N82: 5V_Di_GND63.DOut, 5V_Di_GND64.DIn
  N83: 5V_Di_GND64.DOut, 5V_Di_GND65.DIn
  N84: 5V_Di_GND65.DOut, 5V_Di_GND66.DIn
  N85: 5V_Di_GND70.DIn, 5V_Di_GND69.DOut
  N86: 5V_Di_GND69.DIn, 5V_Di_GND68.DOut
  N87: 5V_Di_GND68.DIn, 5V_Di_GND67.DOut
  N88: 5V_Di_GND67.DIn, 5V_Di_GND66.DOut
  N89: 5V_Di_GND73.DOut, 5V_Di_GND74.DIn
  N90: 5V_Di_GND74.DOut, 5V_Di_GND75.DIn
  N91: 5V_Di_GND75.DOut, 5V_Di_GND76.DIn
  N92: 5V_Di_GND76.DOut, 5V_Di_GND77.DIn
  N93: 5V_Di_GND77.DOut, 5V_Di_GND78.DIn
  N94: 5V_Di_GND78.DOut, 5V_Di_GND79.DIn
  N95: 5V_Di_GND79.DOut, 5V_Di_GND80.DIn
  N96: 5V_Di_GND80.DOut, 5V_Di_GND81.DIn
  N97: 5V_Di_GND81.DOut, 5V_Di_GND82.DIn
  N98: 5V_Di_GND82.DOut, 5V_Di_GND83.DIn
  N99: 5V_Di_GND83.DOut, 5V_Di_GND84.DIn
  GND_2: 5V_Di_GND103.GND, 5V_Di_GND124.GND
  N100: 5V_Di_GND103.DOut, 5V_Di_GND124.DIn
  GND_3: 5V_Di_GND135.GND, 5V_Di_GND146.GND
  N101: 5V_Di_GND135.DOut, 5V_Di_GND146.DIn

notes:
  +
  -
  Gnd
  32K
  SQW
  SCL
  SDA
  3V3
  Power
  5V
  A5
  A4
  D5
  A3
  A2
  TX
  RX
  DT
  SW
  CLK
  D6
  D8
  D9
  D10
  D11
  D12
  A1
  A6
  A7
  Vin
  Rst
  D4
  D3
  D2
  A0
  Aref
  D13
  Signal
  USB
  D7
  Ed Nieuwenhuys 2025
  USB side
  H
  T
  V
  E
  I
  S
  X
  M
  W
  A
  Q

custom parts:
  SMD RGB LED (SK6812): The SK6812 is an RGB LED with a WS2811 control IC built right into the LED.
